// Digital circuit ConventionalAlarmClock.dig as structural Verilog
module ConventionalAlarmClock (
  input  SETUP_TIME,
  input  CLK,
  input  SETUP_ALARM,
  input  ALARM_EN,
  input  CLR,
  input  HR_ADV,
  input  MIN_ADV,
  output [13:0] SEG_SECONDS,
  output [13:0] SEG_MINUTES,
  output [13:0] SEG_HOURS,
  output [5:0] MINUTES,
  output [4:0] HOURS,
  output [5:0] ALARM_MINUTES,
  output BUZZ,
  output [4:0] ALARM_HOURS,
  output [5:0] SECONDS
);

  wire and_1_out, and_2_out, and_3_out, and_4_out, and_5_out, and_6_out, comparator_1_eq, comparator_2_eq,
       not_1_out, not_2_out, not_3_out, not_4_out, xnor_1_out;
  wire [4:0] multiplexer_2_out;
  wire [5:0] multiplexer_1_out, multiplexer_3_out;

  not not_1 (not_1_out, SETUP_ALARM);
  not not_2 (not_2_out, SETUP_TIME);
  xnor xnor_1 (xnor_1_out, SETUP_ALARM, SETUP_TIME);
  and and_1 (and_1_out, SETUP_TIME, not_1_out);
  and and_2 (and_2_out, not_2_out, SETUP_ALARM);
  not not_3 (not_3_out, SETUP_TIME);
  and and_3 (and_3_out, CLK, xnor_1_out);
  and and_4 (and_4_out, and_3_out, CLK);
  and and_5 (and_5_out, SETUP_ALARM, not_3_out);
  // BabylonianClock babylonianclock_1: pin names not known; wires that end beside it: and_4_out, CLR, and_1_out, MIN_ADV, HR_ADV, SECONDS, MINUTES, HOURS
  // BabylonianAlarm babylonianalarm_1: pin names not known; wires that end beside it: CLR, and_2_out, MIN_ADV, HR_ADV, ALARM_HOURS
  Comparator #(.Bits(6)) comparator_1 (.a(MINUTES), .b(ALARM_MINUTES), .eq(comparator_1_eq));  // open: gt, lt
  Comparator #(.Bits(5)) comparator_2 (.a(HOURS), .b(ALARM_HOURS), .eq(comparator_2_eq));  // open: gt, lt
  and and_6 (and_6_out, comparator_1_eq, comparator_2_eq);
  not not_4 (not_4_out, ALARM_EN);
  and and_7 (BUZZ, and_6_out, not_4_out);
  Multiplexer #(.Bits(6)) multiplexer_1 (
    .sel(and_5_out), .in_0(MINUTES), .in_1(ALARM_MINUTES), .out(multiplexer_1_out));
  Multiplexer #(.Bits(5)) multiplexer_2 (.sel(and_5_out), .in_0(HOURS), .in_1(ALARM_HOURS), .out(multiplexer_2_out));
  Multiplexer #(.Bits(6)) multiplexer_3 (.sel(and_5_out), .in_0(SECONDS), .in_1({6{1'b0}}), .out(multiplexer_3_out));
  // SevenSegmentDecoder sevensegmentdecoder_1: pin names not known; wires that end beside it: {1'b0, multiplexer_3_out}, SEG_SECONDS
  // SevenSegmentDecoder sevensegmentdecoder_2: pin names not known; wires that end beside it: {1'b0, multiplexer_1_out}, SEG_MINUTES
  // SevenSegmentDecoder sevensegmentdecoder_3: pin names not known; wires that end beside it: {2'b00, multiplexer_2_out}, SEG_HOURS
endmodule
