// Digital circuit FrenchRepublicanAlarmClock.dig as structural Verilog
module FrenchRepublicanAlarmClock (
  input  CLR,
  input  MIN_ADV,
  input  HR_ADV,
  input  SETUP_ALARM,
  input  SETUP_TIME,
  input  CLK,
  input  ALARM_EN,
  output [6:0] SECONDS,
  output [6:0] MINUTES,
  output [3:0] HOURS,
  output [6:0] ALARM_MINUTES,
  output [3:0] ALARM_HOURS,
  output BUZZ,
  output [13:0] SEG_SECONDS,
  output [13:0] SEG_MINUTES,
  output [13:0] SEG_HOURS
);

  wire and_1_out, and_2_out, and_3_out, and_4_out, and_5_out, and_6_out, and_7_out, and_8_out, and_9_out,
       and_10_out, and_11_out, and_12_out, and_13_out, and_14_out, and_15_out, and_16_out, and_17_out,
       comparator_1_eq, comparator_2_eq, not_1_out, not_2_out, not_3_out, or_1_out, or_2_out, or_3_out,
       or_4_out, or_5_out, or_6_out, or_7_out, or_8_out, or_9_out, or_10_out, xnor_1_out;
  wire [3:0] multiplexer_3_out;
  wire [6:0] multiplexer_1_out, multiplexer_2_out;

  not not_1 (not_1_out, SETUP_ALARM);
  and and_1 (and_1_out, SETUP_TIME, not_1_out);
  not not_2 (not_2_out, SETUP_TIME);
  and and_2 (and_2_out, not_2_out, SETUP_ALARM);
  xnor xnor_1 (xnor_1_out, SETUP_ALARM, SETUP_TIME);
  and and_3 (and_3_out, CLK, xnor_1_out);
  and and_4 (and_4_out, and_3_out, CLK);
  and and_5 (and_5_out, ~and_1_out, and_4_out);  // And
  or or_1 (or_1_out, and_5_out, CLR);
  or or_2 (or_2_out, CLR, and_6_out);
  Counter #(.Bits(7)) SECONDS_COUNTER (.en(1'b1), .C(or_1_out), .clr(or_2_out), .out(SECONDS));  // open: ovf
  Multiplexer #(.Bits(7)) multiplexer_1 (.sel(SETUP_ALARM), .in_0(SECONDS), .in_1({7{1'b0}}), .out(multiplexer_1_out));
  and and_6 (and_6_out, SECONDS[0], SECONDS[1], SECONDS[5], SECONDS[6]);
  or or_3 (or_3_out, and_8_out, CLR);
  or or_4 (or_4_out, CLR, and_9_out);
  and and_7 (and_7_out, ~and_5_out, and_6_out);  // And
  and and_8 (and_8_out, MIN_ADV, and_2_out);
  Counter #(.Bits(7)) MINUTES_COUNTER (.en(1'b1), .C(or_3_out), .clr(or_4_out), .out(ALARM_MINUTES));  // open: ovf
  LookUpTable #(.Bits(14)) SEG_DECODER (
    .in0(multiplexer_1_out[0]), .in1(multiplexer_1_out[1]), .in2(multiplexer_1_out[2]),
    .in3(multiplexer_1_out[3]), .in4(multiplexer_1_out[4]), .in5(multiplexer_1_out[5]),
    .in6(multiplexer_1_out[6]), .out(SEG_SECONDS));
  and and_9 (and_9_out, ALARM_MINUTES[0], ALARM_MINUTES[1], ALARM_MINUTES[5], ALARM_MINUTES[6]);
  and and_10 (and_10_out, MIN_ADV, and_1_out);
  or or_5 (or_5_out, and_10_out, and_7_out, CLR);
  or or_6 (or_6_out, CLR, and_11_out);
  Counter #(.Bits(7)) MINUTES_COUNTER_2 (.en(1'b1), .C(or_5_out), .clr(or_6_out), .out(MINUTES));  // open: ovf
  Multiplexer #(.Bits(7)) multiplexer_2 (
    .sel(SETUP_ALARM), .in_0(MINUTES), .in_1(ALARM_MINUTES), .out(multiplexer_2_out));
  and and_11 (and_11_out, MINUTES[0], MINUTES[1], MINUTES[5], MINUTES[6]);
  and and_12 (and_12_out, HR_ADV, and_2_out);
  or or_7 (or_7_out, and_12_out, CLR);
  or or_8 (or_8_out, CLR, and_14_out);
  and and_13 (and_13_out, ~or_5_out, and_11_out);  // And
  Counter #(.Bits(4)) HOURS_COUNTER (.en(1'b1), .C(or_7_out), .clr(or_8_out), .out(ALARM_HOURS));  // open: ovf
  LookUpTable #(.Bits(14)) SEG_DECODER_2 (
    .in0(multiplexer_2_out[0]), .in1(multiplexer_2_out[1]), .in2(multiplexer_2_out[2]),
    .in3(multiplexer_2_out[3]), .in4(multiplexer_2_out[4]), .in5(multiplexer_2_out[5]),
    .in6(multiplexer_2_out[6]), .out(SEG_MINUTES));
  or or_9 (or_9_out, and_15_out, and_13_out, CLR);
  or or_10 (or_10_out, CLR, and_16_out);
  and and_14 (and_14_out, ALARM_HOURS[0], ALARM_HOURS[3]);
  and and_15 (and_15_out, HR_ADV, and_1_out);
  Counter #(.Bits(4)) HOURS_COUNTER_2 (.en(1'b1), .C(or_9_out), .clr(or_10_out), .out(HOURS));  // open: ovf
  and and_16 (and_16_out, HOURS[0], HOURS[3]);
  Multiplexer #(.Bits(4)) multiplexer_3 (.sel(SETUP_ALARM), .in_0(HOURS), .in_1(ALARM_HOURS), .out(multiplexer_3_out));
  LookUpTable #(.Bits(14)) SEG_DECODER_3 (
    .in0(multiplexer_3_out[0]), .in1(multiplexer_3_out[1]), .in2(multiplexer_3_out[2]),
    .in3(multiplexer_3_out[3]), .in4(1'b0), .in5(1'b0), .in6(1'b0), .out(SEG_HOURS));
  Comparator #(.Bits(7)) comparator_1 (.a(MINUTES), .b(ALARM_MINUTES), .eq(comparator_1_eq));  // open: gt, lt
  Comparator #(.Bits(4)) comparator_2 (.a(HOURS), .b(ALARM_HOURS), .eq(comparator_2_eq));  // open: gt, lt
  and and_17 (and_17_out, comparator_1_eq, comparator_2_eq);
  and and_18 (BUZZ, and_17_out, not_3_out);
  not not_3 (not_3_out, ALARM_EN);

  // Notes on the sheet:
  //   CLK: Hz: 1000
  //   contents of SEG_DECODER (hex, n*v repeats v):
  //   1fbf,1f86,1fdb,1fcf,1fe6,1fed,1ffd,1f87,1fff,1fe7,33f,306,35b
  //   ,34f,366,36d,37d,307,37f,367,2dbf,2d86,2ddb,2dcf,2de6,2ded,2dfd
  //   ,2d87,2dff,2de7,27bf,2786,27db,27cf,27e6,27ed,27fd,2787,27ff,27e7
  //   ,333f,3306,335b,334f,3366,336d,337d,3307,337f,3367,36bf,3686,36db
  //   ,36cf,36e6,36ed,36fd,3687,36ff,36e7,3ebf,3e86,3edb,3ecf,3ee6,3eed
  //   ,3efd,3e87,3eff,3ee7,3bf,386,3db,3cf,3e6,3ed,3fd,387,3ff,3e7,3fbf
  //   ,3f86,3fdb,3fcf,3fe6,3fed,3ffd,3f87,3fff,3fe7,33bf,3386,33db,33cf
  //   ,33e6,33ed,33fd,3387,33ff,33e7
  //   contents of SEG_DECODER_2 (hex, n*v repeats v):
  //   1fbf,1f86,1fdb,1fcf,1fe6,1fed,1ffd,1f87,1fff,1fe7,33f,306,35b
  //   ,34f,366,36d,37d,307,37f,367,2dbf,2d86,2ddb,2dcf,2de6,2ded,2dfd
  //   ,2d87,2dff,2de7,27bf,2786,27db,27cf,27e6,27ed,27fd,2787,27ff,27e7
  //   ,333f,3306,335b,334f,3366,336d,337d,3307,337f,3367,36bf,3686,36db
  //   ,36cf,36e6,36ed,36fd,3687,36ff,36e7,3ebf,3e86,3edb,3ecf,3ee6,3eed
  //   ,3efd,3e87,3eff,3ee7,3bf,386,3db,3cf,3e6,3ed,3fd,387,3ff,3e7,3fbf
  //   ,3f86,3fdb,3fcf,3fe6,3fed,3ffd,3f87,3fff,3fe7,33bf,3386,33db,33cf
  //   ,33e6,33ed,33fd,3387,33ff,33e7
  //   contents of SEG_DECODER_3 (hex, n*v repeats v):
  //   1fbf,1f86,1fdb,1fcf,1fe6,1fed,1ffd,1f87,1fff,1fe7,33f,306,35b
  //   ,34f,366,36d,37d,307,37f,367,2dbf,2d86,2ddb,2dcf,2de6,2ded,2dfd
  //   ,2d87,2dff,2de7,27bf,2786,27db,27cf,27e6,27ed,27fd,2787,27ff,27e7
  //   ,333f,3306,335b,334f,3366,336d,337d,3307,337f,3367,36bf,3686,36db
  //   ,36cf,36e6,36ed,36fd,3687,36ff,36e7,3ebf,3e86,3edb,3ecf,3ee6,3eed
  //   ,3efd,3e87,3eff,3ee7,3bf,386,3db,3cf,3e6,3ed,3fd,387,3ff,3e7,3fbf
  //   ,3f86,3fdb,3fcf,3fe6,3fed,3ffd,3f87,3fff,3fe7,33bf,3386,33db,33cf
  //   ,33e6,33ed,33fd,3387,33ff,33e7
endmodule
