// Digital circuit FrenchRepublicanCalendarAlarmClock.dig as structural Verilog
module FrenchRepublicanCalendarAlarmClock (
  input  CLR,
  input  MIN_ADV,
  input  HR_ADV,
  input  SETUP_ALARM,
  input  SETUP_TIME,
  input  CLK,
  input  ALARM_EN,
  input  DAY_ADV,
  input  WEEK_ADV,
  input  MONTH_ADV,
  input  YEAR_ADV,
  output [6:0] SECONDS,
  output [6:0] MINUTES,
  output [3:0] HOURS,
  output [6:0] ALARM_MINUTES,
  output [3:0] ALARM_HOURS,
  output [13:0] SEG_SECONDS,
  output [13:0] SEG_MINUTES,
  output [13:0] SEG_HOURS,
  output [3:0] DAYS,
  output [13:0] SEG_DAYS,
  output [1:0] WEEKS,
  output [13:0] SEG_WEEKS,
  output [3:0] MONTHS,
  output [13:0] SEG_MONTHS,
  output [3:0] ALARM_DAYS,
  output [1:0] ALARM_WEEKS,
  output [3:0] ALARM_MONTHS,
  output BUZZ,
  output [3:0] YEARS,
  output [13:0] SEG_YEARS
);

  wire and_1_out, and_2_out, and_3_out, and_4_out, and_5_out, and_6_out, and_7_out, and_8_out, and_9_out,
       and_10_out, and_11_out, and_12_out, and_13_out, and_14_out, and_15_out, and_16_out, and_17_out,
       and_18_out, and_19_out, and_20_out, and_21_out, and_22_out, and_23_out, and_24_out, and_25_out,
       and_26_out, and_27_out, and_28_out, and_29_out, and_30_out, and_31_out, and_32_out, and_33_out,
       and_34_out, and_35_out, and_36_out, and_37_out, and_38_out, comparator_1_eq, comparator_2_eq,
       comparator_3_eq, comparator_4_eq, comparator_5_eq, multiplexer_5_out, multiplexer_6_out, not_1_out,
       not_2_out, not_3_out, not_4_out, or_1_out, or_2_out, or_3_out, or_4_out, or_5_out, or_6_out, or_7_out,
       or_8_out, or_9_out, or_10_out, or_11_out, or_12_out, or_13_out, or_14_out, or_15_out, or_16_out,
       or_17_out, or_18_out, or_19_out, or_20_out, or_21_out, or_22_out, or_23_out, or_24_out, xnor_1_out;
  wire [1:0] multiplexer_7_out;
  wire [3:0] multiplexer_3_out, multiplexer_4_out, multiplexer_8_out;
  wire [6:0] multiplexer_1_out, multiplexer_2_out;

  not not_1 (not_1_out, SETUP_TIME);
  and and_1 (and_1_out, SETUP_TIME, not_2_out);
  not not_2 (not_2_out, SETUP_ALARM);
  not not_3 (not_3_out, SETUP_TIME);
  xnor xnor_1 (xnor_1_out, SETUP_ALARM, SETUP_TIME);
  and and_2 (and_2_out, not_1_out, not_3_out);
  and and_3 (and_3_out, not_3_out, SETUP_ALARM);
  and and_4 (and_4_out, CLK, xnor_1_out);
  and and_5 (and_5_out, CLK, and_2_out);
  and and_6 (and_6_out, and_4_out, and_5_out);
  and and_7 (and_7_out, ~and_1_out, and_6_out);  // And
  or or_1 (or_1_out, and_7_out, CLR);
  or or_2 (or_2_out, CLR, and_8_out);
  Counter #(.Bits(7)) SECONDS_COUNTER (.en(1'b1), .C(or_1_out), .clr(or_2_out), .out(SECONDS));  // open: ovf
  or or_3 (or_3_out, CLR, and_12_out);
  Multiplexer #(.Bits(7)) multiplexer_1 (.sel(SETUP_ALARM), .in_0(SECONDS), .in_1({7{1'b0}}), .out(multiplexer_1_out));
  and and_8 (and_8_out, SECONDS[0], SECONDS[1], SECONDS[5], SECONDS[6]);
  and and_9 (and_9_out, MIN_ADV, and_3_out);
  or or_4 (or_4_out, and_9_out, CLR);
  and and_10 (and_10_out, ~and_7_out, and_8_out);  // And
  Counter #(.Bits(7)) MINUTES_COUNTER (.en(1'b1), .C(or_4_out), .clr(or_3_out), .out(ALARM_MINUTES));  // open: ovf
  LookUpTable #(.Bits(14)) SEG_DECODER (
    .in0(multiplexer_1_out[0]), .in1(multiplexer_1_out[1]), .in2(multiplexer_1_out[2]),
    .in3(multiplexer_1_out[3]), .in4(multiplexer_1_out[4]), .in5(multiplexer_1_out[5]),
    .in6(multiplexer_1_out[6]), .out(SEG_SECONDS));
  and and_11 (and_11_out, MIN_ADV, and_1_out);
  or or_5 (or_5_out, and_11_out, and_10_out, CLR);
  or or_6 (or_6_out, CLR, and_13_out);
  and and_12 (and_12_out, ALARM_MINUTES[0], ALARM_MINUTES[1], ALARM_MINUTES[5], ALARM_MINUTES[6]);
  Counter #(.Bits(7)) MINUTES_COUNTER_2 (.en(1'b1), .C(or_5_out), .clr(or_6_out), .out(MINUTES));  // open: ovf
  Multiplexer #(.Bits(7)) multiplexer_2 (
    .sel(SETUP_ALARM), .in_0(MINUTES), .in_1(ALARM_MINUTES), .out(multiplexer_2_out));
  and and_13 (and_13_out, MINUTES[0], MINUTES[1], MINUTES[5], MINUTES[6]);
  and and_14 (and_14_out, ~or_5_out, and_13_out);  // And
  LookUpTable #(.Bits(14)) SEG_DECODER_2 (
    .in0(multiplexer_2_out[0]), .in1(multiplexer_2_out[1]), .in2(multiplexer_2_out[2]),
    .in3(multiplexer_2_out[3]), .in4(multiplexer_2_out[4]), .in5(multiplexer_2_out[5]),
    .in6(multiplexer_2_out[6]), .out(SEG_MINUTES));
  or or_7 (or_7_out, and_15_out, CLR);
  or or_8 (or_8_out, CLR, and_17_out);
  and and_15 (and_15_out, HR_ADV, and_3_out);
  Counter #(.Bits(4)) HOURS_COUNTER (.en(1'b1), .C(or_7_out), .clr(or_8_out), .out(ALARM_HOURS));  // open: ovf
  and and_16 (and_16_out, HR_ADV, and_1_out);
  or or_9 (or_9_out, and_16_out, and_14_out, CLR);
  or or_10 (or_10_out, CLR, and_18_out);
  Counter #(.Bits(4)) HOURS_COUNTER_2 (.en(1'b1), .C(or_9_out), .clr(or_10_out), .out(HOURS));  // open: ovf
  and and_17 (and_17_out, ALARM_HOURS[0], ALARM_HOURS[3]);
  Multiplexer #(.Bits(4)) multiplexer_3 (.sel(SETUP_ALARM), .in_0(HOURS), .in_1(ALARM_HOURS), .out(multiplexer_3_out));
  and and_18 (and_18_out, HOURS[0], HOURS[3]);
  and and_19 (and_19_out, ~or_9_out, and_18_out);  // And
  LookUpTable #(.Bits(14)) SEG_DECODER_3 (
    .in0(multiplexer_3_out[0]), .in1(multiplexer_3_out[1]), .in2(multiplexer_3_out[2]),
    .in3(multiplexer_3_out[3]), .in4(1'b0), .in5(1'b0), .in6(1'b0), .out(SEG_HOURS));
  or or_11 (or_11_out, and_21_out, CLR);
  or or_12 (or_12_out, CLR, and_22_out);
  and and_20 (and_20_out, DAY_ADV, and_1_out);
  or or_13 (or_13_out, and_20_out, and_19_out, CLR);
  or or_14 (or_14_out, CLR, and_23_out);
  and and_21 (and_21_out, DAY_ADV, and_3_out);
  Counter #(.Bits(4)) DAYS_COUNTER (.en(1'b1), .C(or_11_out), .clr(or_12_out), .out(ALARM_DAYS));  // open: ovf
  Counter #(.Bits(4)) DAYS_COUNTER_2 (.en(1'b1), .C(or_13_out), .clr(or_14_out), .out(DAYS));  // open: ovf
  and and_22 (and_22_out, ALARM_DAYS[0], ALARM_DAYS[3]);
  and and_23 (and_23_out, multiplexer_6_out, multiplexer_5_out);
  Multiplexer #(.Bits(4)) multiplexer_4 (.sel(SETUP_ALARM), .in_0(DAYS), .in_1(ALARM_DAYS), .out(multiplexer_4_out));
  and and_24 (and_24_out, ~or_13_out, and_23_out);  // And
  Multiplexer multiplexer_5 (.sel(and_31_out), .in_0(DAYS[2]), .in_1(DAYS[3]), .out(multiplexer_5_out));
  LookUpTable #(.Bits(14)) SEG_DECODER_4 (
    .in0(multiplexer_4_out[0]), .in1(multiplexer_4_out[1]), .in2(multiplexer_4_out[2]),
    .in3(multiplexer_4_out[3]), .in4(1'b0), .in5(1'b0), .in6(1'b0), .out(SEG_DAYS));
  Multiplexer multiplexer_6 (.sel(and_31_out), .in_0(DAYS[0]), .in_1(DAYS[0]), .out(multiplexer_6_out));
  and and_25 (and_25_out, WEEK_ADV, and_3_out);
  or or_15 (or_15_out, and_25_out, CLR);
  or or_16 (or_16_out, CLR, ALARM_WEEKS[1]);
  and and_26 (and_26_out, WEEK_ADV, and_1_out);
  or or_17 (or_17_out, and_26_out, and_24_out, CLR);
  or or_18 (or_18_out, CLR, WEEKS[1]);
  Counter #(.Bits(2)) WEEKS_COUNTER (.en(1'b1), .C(or_15_out), .clr(or_16_out), .out(ALARM_WEEKS));  // open: ovf
  Counter #(.Bits(2)) WEEKS_COUNTER_2 (.en(1'b1), .C(or_17_out), .clr(or_18_out), .out(WEEKS));  // open: ovf
  Multiplexer #(.Bits(2)) multiplexer_7 (.sel(SETUP_ALARM), .in_0(WEEKS), .in_1(ALARM_WEEKS), .out(multiplexer_7_out));
  LookUpTable #(.Bits(14)) SEG_DECODER_5 (
    .in0(multiplexer_7_out[0]), .in1(multiplexer_7_out[1]), .in2(1'b0), .in3(1'b0), .in4(1'b0), .in5(1'b0),
    .in6(1'b0), .out(SEG_WEEKS));
  and and_27 (and_27_out, ~or_17_out, WEEKS[1]);  // And
  or or_19 (or_19_out, and_28_out, CLR);
  or or_20 (or_20_out, CLR, and_30_out);
  and and_28 (and_28_out, MONTH_ADV, and_3_out);
  Counter #(.Bits(4)) MONTHS_COUNTER (.en(1'b1), .C(or_19_out), .clr(or_20_out), .out(ALARM_MONTHS));  // open: ovf
  and and_29 (and_29_out, MONTH_ADV, and_1_out);
  or or_21 (or_21_out, and_29_out, and_27_out, CLR);
  or or_22 (or_22_out, CLR, and_31_out);
  Counter #(.Bits(4)) MONTHS_COUNTER_2 (.en(1'b1), .C(or_21_out), .clr(or_22_out), .out(MONTHS));  // open: ovf
  and and_30 (and_30_out, ALARM_MONTHS[0], ALARM_MONTHS[1], ALARM_MONTHS[3]);
  Multiplexer #(.Bits(4)) multiplexer_8 (
    .sel(SETUP_ALARM), .in_0(MONTHS), .in_1(ALARM_MONTHS), .out(multiplexer_8_out));
  and and_31 (and_31_out, MONTHS[2], MONTHS[3]);
  LookUpTable #(.Bits(14)) SEG_DECODER_6 (
    .in0(multiplexer_8_out[0]), .in1(multiplexer_8_out[1]), .in2(multiplexer_8_out[2]),
    .in3(multiplexer_8_out[3]), .in4(1'b0), .in5(1'b0), .in6(1'b0), .out(SEG_MONTHS));
  and and_32 (and_32_out, ~or_21_out, and_31_out);  // And
  and and_33 (and_33_out, YEAR_ADV, and_1_out);
  or or_23 (or_23_out, and_33_out, and_32_out, CLR);
  or or_24 (or_24_out, CLR, and_34_out);
  Counter #(.Bits(4)) YEARS_COUNTER (.en(1'b1), .C(or_23_out), .clr(or_24_out), .out(YEARS));  // open: ovf
  and and_34 (and_34_out, YEARS[3], YEARS[2]);
  LookUpTable #(.Bits(14)) SEG_DECODER_7 (
    .in0(YEARS[0]), .in1(YEARS[1]), .in2(YEARS[2]), .in3(YEARS[3]), .in4(1'b0), .in5(1'b0), .in6(1'b0),
    .out(SEG_YEARS));
  Comparator #(.Bits(4)) comparator_1 (.a(MONTHS), .b(ALARM_MONTHS), .eq(comparator_1_eq));  // open: gt, lt
  Comparator #(.Bits(2)) comparator_2 (.a(WEEKS), .b(ALARM_WEEKS), .eq(comparator_2_eq));  // open: gt, lt
  Comparator #(.Bits(4)) comparator_3 (.a(DAYS), .b(ALARM_DAYS), .eq(comparator_3_eq));  // open: gt, lt
  Comparator #(.Bits(7)) comparator_4 (.a(MINUTES), .b(ALARM_MINUTES), .eq(comparator_4_eq));  // open: gt, lt
  Comparator #(.Bits(4)) comparator_5 (.a(HOURS), .b(ALARM_HOURS), .eq(comparator_5_eq));  // open: gt, lt
  and and_35 (and_35_out, comparator_4_eq, comparator_5_eq);
  and and_36 (and_36_out, comparator_1_eq, comparator_2_eq);
  and and_37 (and_37_out, and_36_out, comparator_3_eq);
  and and_38 (and_38_out, and_35_out, not_4_out);
  not not_4 (not_4_out, ALARM_EN);
  and and_39 (BUZZ, and_37_out, and_38_out);

  // Notes on the sheet:
  //   contents of SEG_DECODER (hex, n*v repeats v):
  //   1fbf,1f86,1fdb,1fcf,1fe6,1fed,1ffd,1f87,1fff,1fe7,33f,306,35b
  //   ,34f,366,36d,37d,307,37f,367,2dbf,2d86,2ddb,2dcf,2de6,2ded,2dfd
  //   ,2d87,2dff,2de7,27bf,2786,27db,27cf,27e6,27ed,27fd,2787,27ff,27e7
  //   ,333f,3306,335b,334f,3366,336d,337d,3307,337f,3367,36bf,3686,36db
  //   ,36cf,36e6,36ed,36fd,3687,36ff,36e7,3ebf,3e86,3edb,3ecf,3ee6,3eed
  //   ,3efd,3e87,3eff,3ee7,3bf,386,3db,3cf,3e6,3ed,3fd,387,3ff,3e7,3fbf
  //   ,3f86,3fdb,3fcf,3fe6,3fed,3ffd,3f87,3fff,3fe7,33bf,3386,33db,33cf
  //   ,33e6,33ed,33fd,3387,33ff,33e7
  //   contents of SEG_DECODER_2 (hex, n*v repeats v):
  //   1fbf,1f86,1fdb,1fcf,1fe6,1fed,1ffd,1f87,1fff,1fe7,33f,306,35b
  //   ,34f,366,36d,37d,307,37f,367,2dbf,2d86,2ddb,2dcf,2de6,2ded,2dfd
  //   ,2d87,2dff,2de7,27bf,2786,27db,27cf,27e6,27ed,27fd,2787,27ff,27e7
  //   ,333f,3306,335b,334f,3366,336d,337d,3307,337f,3367,36bf,3686,36db
  //   ,36cf,36e6,36ed,36fd,3687,36ff,36e7,3ebf,3e86,3edb,3ecf,3ee6,3eed
  //   ,3efd,3e87,3eff,3ee7,3bf,386,3db,3cf,3e6,3ed,3fd,387,3ff,3e7,3fbf
  //   ,3f86,3fdb,3fcf,3fe6,3fed,3ffd,3f87,3fff,3fe7,33bf,3386,33db,33cf
  //   ,33e6,33ed,33fd,3387,33ff,33e7
  //   contents of SEG_DECODER_3 (hex, n*v repeats v):
  //   1fbf,1f86,1fdb,1fcf,1fe6,1fed,1ffd,1f87,1fff,1fe7,33f,306,35b
  //   ,34f,366,36d,37d,307,37f,367,2dbf,2d86,2ddb,2dcf,2de6,2ded,2dfd
  //   ,2d87,2dff,2de7,27bf,2786,27db,27cf,27e6,27ed,27fd,2787,27ff,27e7
  //   ,333f,3306,335b,334f,3366,336d,337d,3307,337f,3367,36bf,3686,36db
  //   ,36cf,36e6,36ed,36fd,3687,36ff,36e7,3ebf,3e86,3edb,3ecf,3ee6,3eed
  //   ,3efd,3e87,3eff,3ee7,3bf,386,3db,3cf,3e6,3ed,3fd,387,3ff,3e7,3fbf
  //   ,3f86,3fdb,3fcf,3fe6,3fed,3ffd,3f87,3fff,3fe7,33bf,3386,33db,33cf
  //   ,33e6,33ed,33fd,3387,33ff,33e7
  //   contents of SEG_DECODER_4 (hex, n*v repeats v):
  //   1fbf,1f86,1fdb,1fcf,1fe6,1fed,1ffd,1f87,1fff,1fe7,33f,306,35b
  //   ,34f,366,36d,37d,307,37f,367,2dbf,2d86,2ddb,2dcf,2de6,2ded,2dfd
  //   ,2d87,2dff,2de7,27bf,2786,27db,27cf,27e6,27ed,27fd,2787,27ff,27e7
  //   ,333f,3306,335b,334f,3366,336d,337d,3307,337f,3367,36bf,3686,36db
  //   ,36cf,36e6,36ed,36fd,3687,36ff,36e7,3ebf,3e86,3edb,3ecf,3ee6,3eed
  //   ,3efd,3e87,3eff,3ee7,3bf,386,3db,3cf,3e6,3ed,3fd,387,3ff,3e7,3fbf
  //   ,3f86,3fdb,3fcf,3fe6,3fed,3ffd,3f87,3fff,3fe7,33bf,3386,33db,33cf
  //   ,33e6,33ed,33fd,3387,33ff,33e7
  //   contents of SEG_DECODER_5 (hex, n*v repeats v):
  //   1fbf,1f86,1fdb,1fcf,1fe6,1fed,1ffd,1f87,1fff,1fe7,33f,306,35b
  //   ,34f,366,36d,37d,307,37f,367,2dbf,2d86,2ddb,2dcf,2de6,2ded,2dfd
  //   ,2d87,2dff,2de7,27bf,2786,27db,27cf,27e6,27ed,27fd,2787,27ff,27e7
  //   ,333f,3306,335b,334f,3366,336d,337d,3307,337f,3367,36bf,3686,36db
  //   ,36cf,36e6,36ed,36fd,3687,36ff,36e7,3ebf,3e86,3edb,3ecf,3ee6,3eed
  //   ,3efd,3e87,3eff,3ee7,3bf,386,3db,3cf,3e6,3ed,3fd,387,3ff,3e7,3fbf
  //   ,3f86,3fdb,3fcf,3fe6,3fed,3ffd,3f87,3fff,3fe7,33bf,3386,33db,33cf
  //   ,33e6,33ed,33fd,3387,33ff,33e7
  //   contents of SEG_DECODER_6 (hex, n*v repeats v):
  //   1fbf,1f86,1fdb,1fcf,1fe6,1fed,1ffd,1f87,1fff,1fe7,33f,306,35b
  //   ,34f,366,36d,37d,307,37f,367,2dbf,2d86,2ddb,2dcf,2de6,2ded,2dfd
  //   ,2d87,2dff,2de7,27bf,2786,27db,27cf,27e6,27ed,27fd,2787,27ff,27e7
  //   ,333f,3306,335b,334f,3366,336d,337d,3307,337f,3367,36bf,3686,36db
  //   ,36cf,36e6,36ed,36fd,3687,36ff,36e7,3ebf,3e86,3edb,3ecf,3ee6,3eed
  //   ,3efd,3e87,3eff,3ee7,3bf,386,3db,3cf,3e6,3ed,3fd,387,3ff,3e7,3fbf
  //   ,3f86,3fdb,3fcf,3fe6,3fed,3ffd,3f87,3fff,3fe7,33bf,3386,33db,33cf
  //   ,33e6,33ed,33fd,3387,33ff,33e7
  //   contents of SEG_DECODER_7 (hex, n*v repeats v):
  //   1fbf,1f86,1fdb,1fcf,1fe6,1fed,1ffd,1f87,1fff,1fe7,33f,306,35b
  //   ,34f,366,36d,37d,307,37f,367,2dbf,2d86,2ddb,2dcf,2de6,2ded,2dfd
  //   ,2d87,2dff,2de7,27bf,2786,27db,27cf,27e6,27ed,27fd,2787,27ff,27e7
  //   ,333f,3306,335b,334f,3366,336d,337d,3307,337f,3367,36bf,3686,36db
  //   ,36cf,36e6,36ed,36fd,3687,36ff,36e7,3ebf,3e86,3edb,3ecf,3ee6,3eed
  //   ,3efd,3e87,3eff,3ee7,3bf,386,3db,3cf,3e6,3ed,3fd,387,3ff,3e7,3fbf
  //   ,3f86,3fdb,3fcf,3fe6,3fed,3ffd,3f87,3fff,3fe7,33bf,3386,33db,33cf
  //   ,33e6,33ed,33fd,3387,33ff,33e7
endmodule
